// Logisim project encoder.circ as structural Verilog: 6 circuits, main circuit component
module component (
  input  i_rst,
  input  i_clk,
  input  i_start,
  input  [7:0] i_data,
  output o_en,
  output o_we,
  output o_done,
  output [15:0] o_address,
  output [7:0] o_data
);

  wire [7:0] memories_1_active_zone_o_h, memories_1_input_address;
  wire [8:0] reg_enabler_1_we_bus;
  wire [31:0] memories_1_reg_bus_high, memories_1_reg_bus_low;

  memories memories_1 (
    .i_clk(i_clk), .i_rst(i_rst), .we_bus(reg_enabler_1_we_bus), .i_data(i_data),
    .input_address(memories_1_input_address), .reg_bus_high(memories_1_reg_bus_high),
    .reg_bus_low(memories_1_reg_bus_low), .active_zone_O_H(memories_1_active_zone_o_h));
  controller controller_1 (
    .i_rst(i_rst), .i_clk(i_clk), .i_start(i_start), .o_en(o_en), .o_we(o_we), .o_done(o_done),
    .curr_mem_addr(o_address));
  reg_enabler reg_enabler_1 (.i_clk(i_clk), .curr_mem_addr(o_address), .i_rst(i_rst), .we_bus(reg_enabler_1_we_bus));
  encoder encoder_1 (
    .input_address(memories_1_input_address), .reg_bus_high(memories_1_reg_bus_high),
    .reg_bus_low(memories_1_reg_bus_low), .active_zone_O_H(memories_1_active_zone_o_h), .o_data(o_data));
endmodule

// Mem
module memories (
  input  i_clk,
  input  i_rst,
  input  [8:0] we_bus,
  input  [7:0] i_data,
  output [7:0] input_address,
  output [31:0] reg_bus_high,
  output [31:0] reg_bus_low,
  output [7:0] active_zone_O_H
);

  wire not_1_out;

  not not_1 (not_1_out, i_clk);
  Register Input_address_register (.D(i_data), .en(we_bus[8]), .Q(input_address), .clk(not_1_out), .clr(i_rst));
  Register Zone_7 (.D(i_data), .en(we_bus[7]), .Q(reg_bus_high[31:24]), .clk(not_1_out), .clr(i_rst));
  Register Zone_6 (.D(i_data), .en(we_bus[6]), .Q(reg_bus_high[23:16]), .clk(not_1_out), .clr(i_rst));
  Register Zone_5 (.D(i_data), .en(we_bus[5]), .Q(reg_bus_high[15:8]), .clk(not_1_out), .clr(i_rst));
  Register Zone_4 (.D(i_data), .en(we_bus[4]), .Q(reg_bus_high[7:0]), .clk(not_1_out), .clr(i_rst));
  Register Zone_3 (.D(i_data), .en(we_bus[3]), .Q(reg_bus_low[31:24]), .clk(not_1_out), .clr(i_rst));
  Register Zone_2 (.D(i_data), .en(we_bus[2]), .Q(reg_bus_low[23:16]), .clk(not_1_out), .clr(i_rst));
  Register Zone_1 (.D(i_data), .en(we_bus[1]), .Q(reg_bus_low[15:8]), .clk(not_1_out), .clr(i_rst));
  Register Zone_0 (.D(i_data), .en(we_bus[0]), .Q(reg_bus_low[7:0]), .clk(not_1_out), .clr(i_rst));
  comparator comparator_1 (.zone(reg_bus_high[31:24]), .input_address(input_address), .active_zone(active_zone_O_H[7]));
  comparator comparator_2 (.zone(reg_bus_high[23:16]), .input_address(input_address), .active_zone(active_zone_O_H[6]));
  comparator comparator_3 (.zone(reg_bus_high[15:8]), .input_address(input_address), .active_zone(active_zone_O_H[5]));
  comparator comparator_4 (.zone(reg_bus_high[7:0]), .input_address(input_address), .active_zone(active_zone_O_H[4]));
  comparator comparator_5 (.zone(reg_bus_low[31:24]), .input_address(input_address), .active_zone(active_zone_O_H[3]));
  comparator comparator_6 (.zone(reg_bus_low[23:16]), .input_address(input_address), .active_zone(active_zone_O_H[2]));
  comparator comparator_7 (.zone(reg_bus_low[15:8]), .input_address(input_address), .active_zone(active_zone_O_H[1]));
  comparator comparator_8 (.zone(reg_bus_low[7:0]), .input_address(input_address), .active_zone(active_zone_O_H[0]));
endmodule

module comparator (
  input  [7:0] zone,
  input  [7:0] input_address,
  output active_zone
);

  wire comparator_1_eq, comparator_1_gt, comparator_2_lt, or_1_out;
  wire [7:0] adder_1_out;

  Adder adder_1 (.a(zone), .b(8'h4), .out(adder_1_out));  // open: cin, cout
  Comparator comparator_1 (.a(input_address), .b(zone), .gt(comparator_1_gt), .eq(comparator_1_eq));  // open: lt
  Comparator #(.mode("unsigned")) comparator_2 (
    .a(input_address), .b(adder_1_out), .lt(comparator_2_lt));  // open: gt, eq
  or or_1 (or_1_out, comparator_1_gt, comparator_1_eq);
  and and_1 (active_zone, or_1_out, comparator_2_lt);
endmodule

// Enc
module encoder (
  input  [7:0] input_address,
  input  [31:0] reg_bus_high,
  input  [31:0] reg_bus_low,
  input  [7:0] active_zone_O_H,
  output [7:0] o_data
);

  wire or_1_out;
  wire [1:0] priority_encoder_1_out, priority_encoder_2_out;
  wire [2:0] priority_encoder_3_out;
  wire [3:0] decoder_1_out0;
  wire [7:0] bitselector_1_out, subtractor_1_out;

  Priority_Encoder #(.select(2)) priority_encoder_1 (
    .in0(active_zone_O_H[0]), .in1(active_zone_O_H[1]), .in2(active_zone_O_H[2]), .in3(active_zone_O_H[3]),
    .out(priority_encoder_1_out));
  BitSelector #(.width(32), .group(8)) bitselector_1 (
    .in(reg_bus_low), .out(bitselector_1_out), .sel(priority_encoder_1_out));
  BitSelector #(.width(32), .group(8)) bitselector_2 (
    .in(reg_bus_high), .out(bitselector_1_out), .sel(priority_encoder_2_out));
  Priority_Encoder #(.select(2)) priority_encoder_2 (
    .in0(active_zone_O_H[4]), .in1(active_zone_O_H[5]), .in2(active_zone_O_H[6]), .in3(active_zone_O_H[7]),
    .out(priority_encoder_2_out));
  Subtractor subtractor_1 (.a(input_address), .b(bitselector_1_out), .out(subtractor_1_out));  // open: bin, bout
  Decoder #(.select(2), .enable("false")) decoder_1 (
    .out0(decoder_1_out0[0]), .out1(decoder_1_out0[1]), .out2(decoder_1_out0[2]), .out3(decoder_1_out0[3]),
    .sel(subtractor_1_out[1:0]));
  Priority_Encoder priority_encoder_3 (
    .in0(active_zone_O_H[0]), .in1(active_zone_O_H[1]), .in2(active_zone_O_H[2]), .in3(active_zone_O_H[3]),
    .in4(active_zone_O_H[4]), .in5(active_zone_O_H[5]), .in6(active_zone_O_H[6]), .in7(active_zone_O_H[7]),
    .out(priority_encoder_3_out));  // open: en_in, gs, en_out
  or or_1 (or_1_out, active_zone_O_H[0], active_zone_O_H[1], active_zone_O_H[2], active_zone_O_H[3], active_zone_O_H[4], active_zone_O_H[5], active_zone_O_H[6], active_zone_O_H[7]);
  Multiplexer #(.width(8), .enable("false")) multiplexer_1 (
    .in0(input_address), .in1({1'b1, priority_encoder_3_out, decoder_1_out0}), .out(o_data), .sel(or_1_out));

  // Notes on the sheet:
  //   offset
  //   offset(O-H)
  //   zone_number
endmodule

// REn
module reg_enabler (
  input  i_clk,
  input  [15:0] curr_mem_addr,
  input  i_rst,
  output [8:0] we_bus
);

  wire [3:0] register_1_q;

  Register #(.width(4)) register_1 (.D(curr_mem_addr[3:0]), .Q(register_1_q), .clk(i_clk), .clr(i_rst));  // open: en
  Decoder #(.select(4), .enable("false")) decoder_1 (
    .out0(we_bus[0]), .out1(we_bus[1]), .out2(we_bus[2]), .out3(we_bus[3]), .out4(we_bus[4]),
    .out5(we_bus[5]), .out6(we_bus[6]), .out7(we_bus[7]), .out8(we_bus[8]), .sel(register_1_q));  // open: out9, out10, out11, out12, out13, out14, out15
endmodule

// FSM
module controller (
  input  i_rst,
  input  i_clk,
  input  i_start,
  output o_en,
  output o_we,
  output o_done,
  output [15:0] curr_mem_addr
);


  // Notes on the sheet:
  //   FSM
endmodule
